# Fritzing sketch Schematic (saved by Fritzing 0.9.2b)
breadboards: 1

parts:
  U1 = Module 4 Relais 5V [package="Module 4 Relais 5V"]
  L298N1 = L298N DC motor driver
  M1 = Stepper Motor - Unipolar
  YwRobot_Power_Supply1 = YwRobot Breadboard Power Supply [part_number=545043]
  S1 = SWITCH-MOMENTARY-2 [package=tactile_switch_tall]
  S2 = SWITCH-MOMENTARY-2 [package=tactile_switch_tall]
  KEYPAD1 = Membrane Matrix Keypad  # not connected
  OLED_I2C1 = OLED 128x64 I2C Monochrome Display  # not connected
  Bat1 = battery_holder_single_18650
  Bat2 = battery_holder_single_18650
  R1 = Resistor [tolerance=±5% resistance=220 package="0805 [SMD]"]
  R2 = Resistor [tolerance=±5% resistance=220 package="0805 [SMD]"]
  M2 = DC Motor
  Launchpad2 = TI Launchpad MSP430G2

nets:
  VCC: U1.VCC, YwRobot_Power_Supply1.VCC
  GND: U1.GND, YwRobot_Power_Supply1.GND
  N1: U1.IN1, Launchpad2.p2
  N2: U1.IN2, Launchpad2.p3
  N3: U1.K1-NF, M2.pin_1
  N4: U1.K2-NF, M2.pin_2
  N5: L298N1.OUT1, M1.C
  N6: L298N1.12V, M1.COMMON_2, Bat1.+#1
  N7: L298N1.GND, Bat2.+#0, R1.Pin_1, R2.Pin_1
  N8: L298N1.IN1, Launchpad2.p7
  N9: L298N1.IN2, Launchpad2.p6
  N10: L298N1.IN3, Launchpad2.p5
  N11: L298N1.IN4, Launchpad2.p4
  N12: S1.2, R1.Pin_0, Launchpad2.p8
  N13: S2.2, R2.Pin_0, Launchpad2.p9

custom parts:
  Module 4 Relais 5V: Module 4 Relais 5V 4x SPD-06VDC-SD-C
  L298N DC motor driver: 2x DC motor driver with 78M05 positive voltage regulator (7..35 V) L298N: max 46 V, 2 A Set 5 V Enable jumper to enable 5 V regultor (needed for the L298N) and +5 V output at screw terminal or supply external +5 V at screw terminal Set ENA and/or ENB to +5 V to enable motor permanently or supply ENA and/or ENB with PWM signal IN1 and IN2 set rotation directory for motor A (OUT1/OUT2) IN2 and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
  YwRobot Breadboard Power Supply: The YwRobot Breadboard Power Supply (MB-V2) has two power rails; they can be 5V or 3V3. Power to the module can be provided through the female USB socket or through the A10 (female) 2.1mm power jack.
  Membrane Matrix Keypad: Membrane Matrix 3x4 Keypad
  battery_holder_single_18650: single 18650 battery holder
